# Fritzing sketch 02_3LED_Blink (saved by Fritzing 0.9.4)
breadboards: 1

parts:
  R3 = Resistor [tolerance=±5% resistance=330 package=THT]  # not connected
  LED3 = LED - 5mm [color="Green (570nm)" package="5 mm [THT]"]
  LED1 = LED - 5mm [color="Red (633nm)" package="5 mm [THT]"]
  R2 = Resistor [tolerance=±5% resistance=330 package=THT]
  LED2 = LED - 5mm [color="Blue (525nm)" package="5 mm [THT]"]
  Part1 = Arduino Uno (Rev3)
  R1 = Resistor [tolerance=±5% resistance=330 package=THT]  # not connected

nets:
  N1: LED3.cathode, LED1.cathode, LED2.cathode, Part1.GND
  N2: R2.Pin_0, Part1.D7
  N3: R2.Pin_1, LED2.anode

// code stored in the sketch: 02_3LED_Blink.ino

int led1=5;
int led2=6;
int led3=7;

void setup() {
  // put your setup code here, to run once:
  pinMode(led1, OUTPUT);
  pinMode(led2, OUTPUT);
  pinMode(led3, OUTPUT);

}

void loop() {
  // put your main code here, to run repeatedly:
  digitalWrite(led1, HIGH);
  digitalWrite(led2, LOW);
  digitalWrite(led3, LOW);
  delay(800);
  
  digitalWrite(led1, LOW);
  analogWrite(led2, 2.5);
  digitalWrite(led3, LOW);
  delay(800);

  digitalWrite(led1, LOW);
  digitalWrite(led2, LOW);
  digitalWrite(led3, HIGH);
  delay(800);
  
}
